# Fritzing sketch PCB (saved by Fritzing 0.9.9b)
circuit board: 11cm x 8cm

parts:
  RFID = PN532 Elechouse RFID NFC Module V3
  J1 = Power Jack [package=power_jack_slot]
  spdt = male pin header, 3 pins [form="♂ (male)"]
  UKanan = male pin header, 15 pins [form="♂ (male)"]
  hc04 = male pin header, 4 pins [form="♂ (male)"]
  Buzzer = male pin header, 2 pins [form="♂ (male)"]
  UKiri = male pin header, 15 pins [form="♂ (male)"]
  stepper = male pin header, 6 pins [form="♂ (male)"]

nets:
  GND: RFID.GND, J1.GNDBREAK, J1.GND, spdt.pin2, UKanan.pin2, hc04.pin1, Buzzer.pin1, UKiri.pin2, stepper.pin1
  N1: RFID.VCC, J1.PWR, spdt.pin1, UKanan.pin1, hc04.pin4, stepper.pin6
  N2: RFID.SDA, UKiri.pin11
  N3: RFID.SCL, UKiri.pin14
  N4: RFID.IRQ, UKiri.pin5
  N5: spdt.pin3, UKanan.pin9
  N6: UKanan.pin3, hc04.pin3
  N7: UKanan.pin4, hc04.pin2
  N8: UKanan.pin5, stepper.pin2
  N9: UKanan.pin6, stepper.pin3
  N10: UKanan.pin7, stepper.pin4
  N11: UKanan.pin8, stepper.pin5
  N12: UKanan.pin10, Buzzer.pin2

notes:
  5V
  HC04
  Stepper
  SPDT
  Buzz

custom parts:
  PN532 Elechouse RFID NFC Module V3: NFC is a popular technology in recent years. We often heard this work while smart phone company such as Samsung or HTC introduces their latest high-end phones. Almost all the high-end phone in the market support NFC. Near field communication (NFC) is a set of standards for smart phones and similar devices to establish radio communication with each other by touching them together or bringing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
